# Fritzing sketch Logger (saved by Fritzing 0.8.7b)
breadboards: 1

parts:
  U1 = ESP8266 WiFi Module [part_number=ESP8266]
  Part1 = Arduino Uno (Rev3) - ICSP
  C1 = Capacitor Polarized [package=cpol-radial-100uf-25v]  # not connected
  RHT1 = Humidity and Temperature Sensor RHT03  # not connected
  R1 = Resistor [package="2010 [SMD]"]

nets:
  N1: U1.RXD, Part1.D0/RX
  N2: U1.VCC, U1.CH_PD
  N3: U1.GPIO_0, R1.Pin_0
  N4: U1.GND, Part1.AREF
  N5: U1.TXD, Part1.D1/TX
  N6: Part1.5V, R1.Pin_1

custom parts:
  ESP8266 WiFi Module: Generic WiFi Module based on the ESP8266 with onboard PCB antenna and UART communications
